# Fritzing sketch Ardufarmbot (saved by Fritzing 0.9.3b)
breadboards: 1

parts:
  DHT1 = DHT11 Humitidy and Temperature Sensor
  R1 = Resistor [tolerance=±5% resistance=220 package="2512 [SMD]"]
  LED1 = smd LED [color="Red (633nm)" package="1206 [SMD]"]
  R2 = Resistor [tolerance=±5% resistance=220 package="2512 [SMD]"]
  S1 = Momentary Switch [package=ksa_sealed_tac_switch]
  R3 = Resistor [tolerance=±5% resistance=10k package="2512 [SMD]"]
  Componente1 = Arduino Uno (Rev3) - ICSP
  U4 = 2-Channel 5v Relay Shield [package=relay-2ch5v10a]
  VALVE1 = Plastic Solenoid Valve
  VCC1 = Battery
  LCD_20x5 = LCD screen  # not connected
  IIC4 = IIC Convterter [part_number="LCD 20 x 4" package=converter]
  J5 = Power Jack [part_number="POWER 5V" package=power_jack_smd]
  D1 = Diode [package=diode-1n4148]  # not connected

nets:
  VDD: DHT1.VDD, R1.Pin_1, Componente1.5V
  N1: DHT1.DATA, R1.Pin_0, Componente1.D5_PWM
  GND: DHT1.GND, R3.Pin_1, Componente1.GND
  N2: LED1.anode, R2.Pin_0
  N3: R2.Pin_1, Componente1.D13/SCK
  N4: S1.1, S1.2
  N5: S1.3, S1.4
  N6: R3.Pin_0, Componente1.D11_PWM/MOSI
  N7: Componente1.A4/SDA, IIC4.SDA
  N8: Componente1.A5/SCL, IIC4.SCL
  N9: Componente1.D7, U4.IN2
  VCC: U4.VCC, IIC4.Vcc, J5.GNDBREAK
  GND_2: U4.GND, IIC4.GND, J5.GND
  N10: U4.K2-In, VCC1.+
  N11: U4.K2-On, VALVE1.no_name_yet

custom parts:
  DHT11 Humitidy and Temperature Sensor: DHT11 Humidity and Temperature Sensor
  2-Channel 5v Relay Shield: 2 Channel 5v Relay Shield w. 2x SPD-06VDC-SD-C
  LCD screen: A standard character display, usually with 2x16 characters. Comes in many colors.
  IIC Convterter: Parallel to IIC Converter for HD44780 family LCDs
